// Digital circuit controle_refrigerante_digital.dig as structural Verilog
module controle_refrigerante_digital (
  input  clk,
  input  in_3,
  input  [1:0] in_4,
  input  [1:0] in_5,
  output [1:0] out_1
);

  controle_refrigerante #(.applicationType("GHDL"), .ghdlOptions("--std=93c --ieee=synopsys"), .CodeFile("C:\\Users\\zanel\\Downloads\\controle_refrigerante.vhdl")) u_controle_refrigerante (
    .Clock(clk), .Reset(in_3), .moeda(in_4), .seletorRefrigerante(in_5), .refrigerante(out_1));
endmodule
